# Fritzing sketch PiLOG NRF24 I2C (saved by Fritzing 0.9.3b)
circuit board: 2.8cm x 2.85cm
breadboards: 1

parts:
  J2 = double row female pin header, 16 pins [form="♀ (female)"]
  NRF24 = NRF24L01+ Breakout Board
  C1 = Electrolytic Capacitor [capacitance=1µF package="100 mil [THT, electrolytic]"]
  U1 = ATTINY45 [package=dip]
  R1 = Resistor [tolerance=±5% resistance=10k package=THT]
  R2 = Resistor [tolerance=±5% resistance=4.7k package=THT]
  R3 = Resistor [tolerance=±5% resistance=1k package=THT]
  C2 = Ceramic Capacitor [capacitance=100nF package="100 mil [THT, multilayer]"]
  R4 = Resistor [tolerance=±5% resistance=4.7k package=THT]
  R5 = Resistor [tolerance=±5% resistance=4.7k package=THT]

nets:
  GND: J2.pin1, J2.pin10, J2.pin13, NRF24.GND, C1.-, U1.GND, C2.1
  VCC: J2.pin5, NRF24.VCC, C1.+, U1.VCC, R1.Pin_0, R4.Pin_0, R5.Pin_0
  N1: J2.pin11, U1.PB0(MOSI), R4.Pin_1
  N2: J2.pin12, U1.PB2(SCK_ADC1), R5.Pin_1
  N3: NRF24.CE, NRF24.CS, R3.Pin_0, C2.0
  N4: NRF24.SCK, U1.PB3(ADC3), R3.Pin_1
  N5: NRF24.MOSI, U1.PB4(ADC2), R2.Pin_0
  N6: NRF24.MISO, R2.Pin_1
  N7: U1.PB5(NRES), R1.Pin_1

notes:
  OPiLOG
  NRF24 Extensor
